// Logisim project fahriyegun_pro1.circ as structural Verilog: 13 circuits, main circuit main
module main (
  input  clock
);

  wire cpu_1_mem_ld;
  wire [11:0] cpu_1_mem_address;
  wire [15:0] cpu_1_mem_datain, ram_1_data;

  CPU cpu_1 (
    .CLOCK(clock), .mem_out(ram_1_data), .mem_address(cpu_1_mem_address), .mem_datain(cpu_1_mem_datain),
    .mem_ld(cpu_1_mem_ld));
  RAM #(.addrWidth(12), .dataWidth(16), .bus("separate")) ram_1 (
    .addr(cpu_1_mem_address), .din(cpu_1_mem_datain), .data(ram_1_data), .str(cpu_1_mem_ld), .sel(1'b1),
    .clk(clock), .ld(1'b1), .clr(1'b0));

  // Notes on the sheet:
  //   MEMORY
endmodule

module reg16bit (
  input  clock,
  input  regld,
  input  [15:0] _16bit_input,
  output [15:0] _16bit_output
);

  wire not_1_out, not_2_out, not_3_out, not_4_out, not_5_out, not_6_out, not_7_out, not_8_out, not_9_out,
       not_10_out, not_11_out, not_12_out, not_13_out, not_14_out, not_15_out, not_16_out;

  not not_1 (not_1_out, _16bit_input[0]);
  not not_2 (not_2_out, _16bit_input[1]);
  not not_3 (not_3_out, _16bit_input[2]);
  not not_4 (not_4_out, _16bit_input[3]);
  not not_5 (not_5_out, _16bit_input[4]);
  not not_6 (not_6_out, _16bit_input[5]);
  not not_7 (not_7_out, _16bit_input[6]);
  not not_8 (not_8_out, _16bit_input[7]);
  not not_9 (not_9_out, _16bit_input[8]);
  not not_10 (not_10_out, _16bit_input[9]);
  not not_11 (not_11_out, _16bit_input[10]);
  not not_12 (not_12_out, _16bit_input[11]);
  not not_13 (not_13_out, _16bit_input[12]);
  not not_14 (not_14_out, _16bit_input[13]);
  not not_15 (not_15_out, _16bit_input[14]);
  not not_16 (not_16_out, _16bit_input[15]);
  S_R_Flip_Flop s_r_ff_1 (
    .S(_16bit_input[0]), .clk(clock), .R(not_1_out), .Q(_16bit_output[0]), .en(regld));  // open: Qn, preset, reset
  S_R_Flip_Flop s_r_ff_2 (
    .S(_16bit_input[1]), .clk(clock), .R(not_2_out), .Q(_16bit_output[1]), .en(regld));  // open: Qn, preset, reset
  S_R_Flip_Flop s_r_ff_3 (
    .S(_16bit_input[2]), .clk(clock), .R(not_3_out), .Q(_16bit_output[2]), .en(regld));  // open: Qn, preset, reset
  S_R_Flip_Flop s_r_ff_4 (
    .S(_16bit_input[3]), .clk(clock), .R(not_4_out), .Q(_16bit_output[3]), .en(regld));  // open: Qn, preset, reset
  S_R_Flip_Flop s_r_ff_5 (
    .S(_16bit_input[4]), .clk(clock), .R(not_5_out), .Q(_16bit_output[4]), .en(regld));  // open: Qn, preset, reset
  S_R_Flip_Flop s_r_ff_6 (
    .S(_16bit_input[5]), .clk(clock), .R(not_6_out), .Q(_16bit_output[5]), .en(regld));  // open: Qn, preset, reset
  S_R_Flip_Flop s_r_ff_7 (
    .S(_16bit_input[6]), .clk(clock), .R(not_7_out), .Q(_16bit_output[6]), .en(regld));  // open: Qn, preset, reset
  S_R_Flip_Flop s_r_ff_8 (
    .S(_16bit_input[7]), .clk(clock), .R(not_8_out), .Q(_16bit_output[7]), .en(regld));  // open: Qn, preset, reset
  S_R_Flip_Flop s_r_ff_9 (
    .S(_16bit_input[8]), .clk(clock), .R(not_9_out), .Q(_16bit_output[8]), .en(regld));  // open: Qn, preset, reset
  S_R_Flip_Flop s_r_ff_10 (
    .S(_16bit_input[9]), .clk(clock), .R(not_10_out), .Q(_16bit_output[9]), .en(regld));  // open: Qn, preset, reset
  S_R_Flip_Flop s_r_ff_11 (
    .S(_16bit_input[10]), .clk(clock), .R(not_11_out), .Q(_16bit_output[10]), .en(regld));  // open: Qn, preset, reset
  S_R_Flip_Flop s_r_ff_12 (
    .S(_16bit_input[11]), .clk(clock), .R(not_12_out), .Q(_16bit_output[11]), .en(regld));  // open: Qn, preset, reset
  S_R_Flip_Flop s_r_ff_13 (
    .S(_16bit_input[12]), .clk(clock), .R(not_13_out), .Q(_16bit_output[12]), .en(regld));  // open: Qn, preset, reset
  S_R_Flip_Flop s_r_ff_14 (
    .S(_16bit_input[13]), .clk(clock), .R(not_14_out), .Q(_16bit_output[13]), .en(regld));  // open: Qn, preset, reset
  S_R_Flip_Flop s_r_ff_15 (
    .S(_16bit_input[14]), .clk(clock), .R(not_15_out), .Q(_16bit_output[14]), .en(regld));  // open: Qn, preset, reset
  S_R_Flip_Flop s_r_ff_16 (
    .S(_16bit_input[15]), .clk(clock), .R(not_16_out), .Q(_16bit_output[15]), .en(regld));  // open: Qn, preset, reset
endmodule

module reg7SP (
  input  regld,
  input  inc,
  input  dec,
  input  clock,
  input  [15:0] _16bit_input_sp,
  output [15:0] _16bit_output_sp
);

  wire or_1_out;
  wire [15:0] adder_1_out, multiplexer_1_out, subtractor_1_out;

  Adder #(.width(16)) adder_1 (.a(_16bit_output_sp), .b(16'h1), .out(adder_1_out));  // open: cin, cout
  Subtractor #(.width(16)) subtractor_1 (.a(_16bit_output_sp), .b(16'h1), .out(subtractor_1_out));  // open: bin, bout
  Multiplexer #(.select(2), .width(16), .enable("false")) multiplexer_1 (
    .in0(_16bit_input_sp), .in1(adder_1_out), .in2(subtractor_1_out), .in3({16{1'b0}}),
    .out(multiplexer_1_out), .sel({dec, inc}));
  or or_1 (or_1_out, dec, inc, regld);
  reg16bit reg16bit_1 (
    .regld(or_1_out), ._16bit_input(multiplexer_1_out), .clock(clock), ._16bit_output(_16bit_output_sp));
endmodule

module RegBank (
  input  clock,
  input  [15:0] data_in,
  input  [2:0] reg_sel,
  input  regld,
  input  sp_plus_plus,
  input  sp_minus_minus,
  output [15:0] Reg0,
  output [15:0] Reg1,
  output [15:0] Reg2,
  output [15:0] Reg3,
  output [15:0] Reg4,
  output [15:0] Reg5,
  output [15:0] Reg6,
  output [15:0] Reg7sp
);

  wire and_1_out, and_2_out, and_3_out, and_4_out, and_5_out, and_6_out, and_7_out, and_8_out,
       decoder_1_out0, decoder_1_out1, decoder_1_out2, decoder_1_out3, decoder_1_out4, decoder_1_out5,
       decoder_1_out6, decoder_1_out7, or_1_out, or_2_out;

  Decoder #(.select(3), .enable("false")) decoder_1 (
    .out0(decoder_1_out0), .out1(decoder_1_out1), .out2(decoder_1_out2), .out3(decoder_1_out3),
    .out4(decoder_1_out4), .out5(decoder_1_out5), .out6(decoder_1_out6), .out7(decoder_1_out7), .sel(reg_sel));
  and and_1 (and_1_out, decoder_1_out0, regld);
  and and_2 (and_2_out, decoder_1_out1, regld);
  and and_3 (and_3_out, decoder_1_out2, regld);
  and and_4 (and_4_out, decoder_1_out3, regld);
  and and_5 (and_5_out, decoder_1_out4, regld);
  and and_6 (and_6_out, decoder_1_out5, regld);
  and and_7 (and_7_out, decoder_1_out6, regld);
  and and_8 (and_8_out, decoder_1_out7, regld);
  or or_1 (or_1_out, sp_plus_plus, sp_minus_minus);
  or or_2 (or_2_out, and_8_out, or_1_out);
  reg16bit reg16bit_1 (.regld(and_1_out), ._16bit_input(data_in), .clock(clock), ._16bit_output(Reg0));
  reg16bit reg16bit_2 (.regld(and_2_out), ._16bit_input(data_in), .clock(clock), ._16bit_output(Reg1));
  reg16bit reg16bit_3 (.regld(and_3_out), ._16bit_input(data_in), .clock(clock), ._16bit_output(Reg2));
  reg16bit reg16bit_4 (.regld(and_4_out), ._16bit_input(data_in), .clock(clock), ._16bit_output(Reg3));
  reg16bit reg16bit_5 (.regld(and_5_out), ._16bit_input(data_in), .clock(clock), ._16bit_output(Reg4));
  reg16bit reg16bit_6 (.regld(and_6_out), ._16bit_input(data_in), .clock(clock), ._16bit_output(Reg5));
  reg16bit reg16bit_7 (.regld(and_7_out), ._16bit_input(data_in), .clock(clock), ._16bit_output(Reg6));
  reg7SP reg7sp_1 (
    .regld(or_2_out), .inc(sp_plus_plus), .dec(sp_minus_minus), ._16bit_input_sp(data_in), .clock(clock),
    ._16bit_output_sp(Reg7sp));
endmodule

module reg12bit (
  input  CLK,
  input  [11:0] input_12bit,
  input  LOAD,
  output [11:0] output_12bit
);

  wire not_1_out, not_2_out, not_3_out, not_4_out, not_5_out, not_6_out, not_7_out, not_8_out, not_9_out,
       not_10_out, not_11_out, not_12_out;

  not not_1 (not_1_out, input_12bit[0]);
  not not_2 (not_2_out, input_12bit[1]);
  not not_3 (not_3_out, input_12bit[2]);
  not not_4 (not_4_out, input_12bit[3]);
  not not_5 (not_5_out, input_12bit[4]);
  not not_6 (not_6_out, input_12bit[5]);
  not not_7 (not_7_out, input_12bit[6]);
  not not_8 (not_8_out, input_12bit[7]);
  not not_9 (not_9_out, input_12bit[8]);
  not not_10 (not_10_out, input_12bit[9]);
  not not_11 (not_11_out, input_12bit[10]);
  not not_12 (not_12_out, input_12bit[11]);
  S_R_Flip_Flop s_r_ff_1 (
    .S(input_12bit[0]), .clk(CLK), .R(not_1_out), .Q(output_12bit[0]), .en(LOAD));  // open: Qn, preset, reset
  S_R_Flip_Flop s_r_ff_2 (
    .S(input_12bit[1]), .clk(CLK), .R(not_2_out), .Q(output_12bit[1]), .en(LOAD));  // open: Qn, preset, reset
  S_R_Flip_Flop s_r_ff_3 (
    .S(input_12bit[2]), .clk(CLK), .R(not_3_out), .Q(output_12bit[2]), .en(LOAD));  // open: Qn, preset, reset
  S_R_Flip_Flop s_r_ff_4 (
    .S(input_12bit[3]), .clk(CLK), .R(not_4_out), .Q(output_12bit[3]), .en(LOAD));  // open: Qn, preset, reset
  S_R_Flip_Flop s_r_ff_5 (
    .S(input_12bit[4]), .clk(CLK), .R(not_5_out), .Q(output_12bit[4]), .en(LOAD));  // open: Qn, preset, reset
  S_R_Flip_Flop s_r_ff_6 (
    .S(input_12bit[5]), .clk(CLK), .R(not_6_out), .Q(output_12bit[5]), .en(LOAD));  // open: Qn, preset, reset
  S_R_Flip_Flop s_r_ff_7 (
    .S(input_12bit[6]), .clk(CLK), .R(not_7_out), .Q(output_12bit[6]), .en(LOAD));  // open: Qn, preset, reset
  S_R_Flip_Flop s_r_ff_8 (
    .S(input_12bit[7]), .clk(CLK), .R(not_8_out), .Q(output_12bit[7]), .en(LOAD));  // open: Qn, preset, reset
  S_R_Flip_Flop s_r_ff_9 (
    .S(input_12bit[8]), .clk(CLK), .R(not_9_out), .Q(output_12bit[8]), .en(LOAD));  // open: Qn, preset, reset
  S_R_Flip_Flop s_r_ff_10 (
    .S(input_12bit[9]), .clk(CLK), .R(not_10_out), .Q(output_12bit[9]), .en(LOAD));  // open: Qn, preset, reset
  S_R_Flip_Flop s_r_ff_11 (
    .S(input_12bit[10]), .clk(CLK), .R(not_11_out), .Q(output_12bit[10]), .en(LOAD));  // open: Qn, preset, reset
  S_R_Flip_Flop s_r_ff_12 (
    .S(input_12bit[11]), .clk(CLK), .R(not_12_out), .Q(output_12bit[11]), .en(LOAD));  // open: Qn, preset, reset
endmodule

module IR (
  input  CLK,
  input  [11:0] input_12bit,
  input  LOAD,
  output [5:0] alu_select_11_6,
  output [2:0] src_8_6,
  output [2:0] src_5_3,
  output [2:0] dst_2_0,
  output [11:0] output_12bit
);

  wire not_1_out, not_2_out, not_3_out, not_4_out, not_5_out, not_6_out, not_7_out, not_8_out, not_9_out,
       not_10_out, not_11_out, not_12_out;

  not not_1 (not_1_out, input_12bit[0]);
  not not_2 (not_2_out, input_12bit[1]);
  not not_3 (not_3_out, input_12bit[2]);
  not not_4 (not_4_out, input_12bit[3]);
  not not_5 (not_5_out, input_12bit[4]);
  not not_6 (not_6_out, input_12bit[5]);
  not not_7 (not_7_out, input_12bit[6]);
  not not_8 (not_8_out, input_12bit[7]);
  not not_9 (not_9_out, input_12bit[8]);
  not not_10 (not_10_out, input_12bit[9]);
  not not_11 (not_11_out, input_12bit[10]);
  not not_12 (not_12_out, input_12bit[11]);
  S_R_Flip_Flop s_r_ff_1 (
    .S(input_12bit[0]), .clk(CLK), .R(not_1_out), .Q(dst_2_0[0]), .en(LOAD));  // open: Qn, preset, reset
  S_R_Flip_Flop s_r_ff_2 (
    .S(input_12bit[1]), .clk(CLK), .R(not_2_out), .Q(dst_2_0[1]), .en(LOAD));  // open: Qn, preset, reset
  S_R_Flip_Flop s_r_ff_3 (
    .S(input_12bit[2]), .clk(CLK), .R(not_3_out), .Q(dst_2_0[2]), .en(LOAD));  // open: Qn, preset, reset
  S_R_Flip_Flop s_r_ff_4 (
    .S(input_12bit[3]), .clk(CLK), .R(not_4_out), .Q(output_12bit[3]), .en(LOAD));  // open: Qn, preset, reset
  S_R_Flip_Flop s_r_ff_5 (
    .S(input_12bit[4]), .clk(CLK), .R(not_5_out), .Q(output_12bit[4]), .en(LOAD));  // open: Qn, preset, reset
  S_R_Flip_Flop s_r_ff_6 (
    .S(input_12bit[5]), .clk(CLK), .R(not_6_out), .Q(output_12bit[5]), .en(LOAD));  // open: Qn, preset, reset
  S_R_Flip_Flop s_r_ff_7 (
    .S(input_12bit[6]), .clk(CLK), .R(not_7_out), .Q(alu_select_11_6[0]), .en(LOAD));  // open: Qn, preset, reset
  S_R_Flip_Flop s_r_ff_8 (
    .S(input_12bit[7]), .clk(CLK), .R(not_8_out), .Q(alu_select_11_6[1]), .en(LOAD));  // open: Qn, preset, reset
  S_R_Flip_Flop s_r_ff_9 (
    .S(input_12bit[8]), .clk(CLK), .R(not_9_out), .Q(alu_select_11_6[2]), .en(LOAD));  // open: Qn, preset, reset
  S_R_Flip_Flop s_r_ff_10 (
    .S(input_12bit[9]), .clk(CLK), .R(not_10_out), .Q(alu_select_11_6[3]), .en(LOAD));  // open: Qn, preset, reset
  S_R_Flip_Flop s_r_ff_11 (
    .S(input_12bit[10]), .clk(CLK), .R(not_11_out), .Q(alu_select_11_6[4]), .en(LOAD));  // open: Qn, preset, reset
  S_R_Flip_Flop s_r_ff_12 (
    .S(input_12bit[11]), .clk(CLK), .R(not_12_out), .Q(alu_select_11_6[5]), .en(LOAD));  // open: Qn, preset, reset

  assign {output_12bit[11:6], output_12bit[2:0]} = {alu_select_11_6, dst_2_0};
  assign src_5_3 = output_12bit[5:3];
  assign src_8_6 = alu_select_11_6[2:0];
endmodule

module PC (
  input  clock,
  input  [11:0] pc_in12,
  input  pc_inc,
  input  pc_ld,
  output [11:0] pc_out12
);

  wire or_1_out;
  wire [11:0] adder_1_out, multiplexer_1_out;

  Adder #(.width(12)) adder_1 (.a(pc_out12), .b(12'h1), .out(adder_1_out));  // open: cin, cout
  Multiplexer #(.width(12), .enable("false")) multiplexer_1 (
    .in0(pc_in12), .in1(adder_1_out), .out(multiplexer_1_out), .sel(pc_inc));
  or or_1 (or_1_out, pc_inc, pc_ld);
  reg12bit reg12bit_1 (.input_12bit(multiplexer_1_out), .LOAD(or_1_out), .CLK(clock), .output_12bit(pc_out12));
endmodule

// ZF
module ZeroFlag (
  input  clock,
  input  zf_in,
  input  zfld,
  output zf_out
);

  wire not_1_out;

  not not_1 (not_1_out, zf_in);
  S_R_Flip_Flop s_r_ff_1 (.S(zf_in), .clk(clock), .R(not_1_out), .Q(zf_out), .en(zfld));  // open: Qn, preset, reset
endmodule

module ALU (
  input  [15:0] input1,
  input  [15:0] input2,
  input  [5:0] alu_sel,
  output [15:0] alu_output,
  output ZF
);

  wire and_1_out;
  wire [15:0] adder_1_out, adder_2_out, and_2_out, multiplexer_1_out, multiplexer_3_out, not_1_out, or_1_out,
       subtractor_1_out, subtractor_2_out, xor_1_out;

  Adder #(.width(16)) adder_1 (.a(input1), .b(input2), .out(adder_1_out));  // open: cin, cout
  Subtractor #(.width(16)) subtractor_1 (.a(input1), .b(input1), .out(subtractor_1_out));  // open: bin, bout
  Multiplexer #(.select(3), .width(16), .enable("false")) multiplexer_1 (
    .in0(adder_1_out), .in1(subtractor_1_out), .in2(and_2_out), .in3(or_1_out), .in4(xor_1_out),
    .in5({16{1'b0}}), .in6({16{1'b0}}), .in7({16{1'b0}}), .out(multiplexer_1_out), .sel(alu_sel[5:3]));
  and and_1 (and_1_out, alu_sel[5], alu_sel[4], alu_sel[3]);
  assign and_2_out = input1 & input1;  // AND_Gate and_2, 16 bits wide
  Multiplexer #(.width(16), .enable("false")) multiplexer_2 (
    .in0(multiplexer_1_out), .in1(multiplexer_3_out), .out(alu_output), .sel(and_1_out));
  assign or_1_out = input1 | input1;  // OR_Gate or_1, 16 bits wide
  assign xor_1_out = input1 ^ input1;  // XOR_Gate xor_1, 16 bits wide
  assign not_1_out = ~input2;  // NOT_Gate not_1, 16 bits wide
  Multiplexer #(.select(3), .width(16), .enable("false")) multiplexer_3 (
    .in0(not_1_out), .in1(input2), .in2(adder_2_out), .in3(subtractor_2_out), .in4({16{1'b0}}),
    .in5({16{1'b0}}), .in6({16{1'b0}}), .in7({16{1'b0}}), .out(multiplexer_3_out), .sel(alu_sel[2:0]));
  Adder #(.width(16)) adder_2 (.a(input2), .b(16'h1), .out(adder_2_out));  // open: cin, cout
  nor nor_1 (ZF, alu_output[0], alu_output[1], alu_output[2], alu_output[3], alu_output[4], alu_output[5], alu_output[6], alu_output[7], alu_output[8], alu_output[9], alu_output[10], alu_output[11], alu_output[12], alu_output[13], alu_output[14], alu_output[15]);
  Subtractor #(.width(16)) subtractor_2 (.a(input2), .b(16'h1), .out(subtractor_2_out));  // open: bin, bout
endmodule

module reg4bit (
  input  [3:0] input_4bit,
  input  clk,
  output [3:0] \output 
);

  wire not_1_out, not_2_out, not_3_out, not_4_out;

  S_R_Flip_Flop s_r_ff_1 (
    .S(input_4bit[0]), .clk(clk), .R(not_1_out), .Q(\output [0]), .en(1'b1));  // open: Qn, preset, reset
  not not_1 (not_1_out, input_4bit[0]);
  S_R_Flip_Flop s_r_ff_2 (
    .S(input_4bit[1]), .clk(clk), .R(not_2_out), .Q(\output [1]), .en(1'b1));  // open: Qn, preset, reset
  not not_2 (not_2_out, input_4bit[1]);
  S_R_Flip_Flop s_r_ff_3 (
    .S(input_4bit[2]), .clk(clk), .R(not_3_out), .Q(\output [2]), .en(1'b1));  // open: Qn, preset, reset
  not not_3 (not_3_out, input_4bit[2]);
  S_R_Flip_Flop s_r_ff_4 (
    .S(input_4bit[3]), .clk(clk), .R(not_4_out), .Q(\output [3]), .en(1'b1));  // open: Qn, preset, reset
  not not_4 (not_4_out, input_4bit[3]);
endmodule

// CU
module ControlUnit (
  input  [3:0] opcode,
  input  zf,
  input  clock,
  output IRLD,
  output ZFLD,
  output REGLD,
  output SP_plus_plus,
  output SP_minus_minus,
  output PC_plus_plus,
  output PCLD,
  output [1:0] ARMUX,
  output [2:0] MUX,
  output RETMUX,
  output MEMLD,
  output FETCH
);

  wire not_1_out, not_2_out, not_3_out;
  wire [1:1] and_1_out;
  wire [4:0] multiplexer_1_out, multiplexer_2_out, reg5bit_1_output, rom_1_data;

  not not_1 (not_1_out, opcode[3]);
  not not_2 (not_2_out, opcode[1]);
  and and_1 (and_1_out[1], not_1_out, opcode[2], not_2_out, not_3_out);
  not not_3 (not_3_out, opcode[0]);
  Multiplexer #(.select(2), .width(5), .enable("false")) multiplexer_1 (
    .in0({opcode, 1'b0}), .in1({opcode, 1'b0}), .in2({5{1'b0}}), .in3(5'b01010), .out(multiplexer_1_out),
    .sel({and_1_out[1], zf}));
  Multiplexer #(.width(5), .enable("false")) multiplexer_2 (
    .in0(rom_1_data), .in1(multiplexer_1_out), .out(multiplexer_2_out), .sel(FETCH));
  reg5bit reg5bit_1 (.input_5bit(multiplexer_2_out), .clk(clock), .\output (reg5bit_1_output));
  ROM #(.addrWidth(5), .dataWidth(20)) rom_1 (
    .addr(reg5bit_1_output),
    .data({FETCH, MEMLD, RETMUX, MUX[0], MUX[1], MUX[2], ARMUX[0], ARMUX[1], PCLD, PC_plus_plus, SP_minus_minus, SP_plus_plus, REGLD, ZFLD, IRLD, rom_1_data}));  // open: sel

  // Notes on the sheet:
  //   isJmp
  //   0 0101(jmp)
  //   contents of rom_1 (hex, n*v repeats v):
  //   80420 0 480 0 2080 0 52000 0 0 0 800 0 0 0 18080 0 51200 0 113 1080 45a00 0 117 21800
endmodule

module CPU (
  input  CLOCK,
  input  [15:0] mem_out,
  output [11:0] mem_address,
  output [15:0] mem_datain,
  output mem_ld
);

  wire alu_1_zf, controlunit_1_irld, controlunit_1_pc_plus_plus, controlunit_1_pcld, controlunit_1_regld,
       controlunit_1_retmux, controlunit_1_sp_minus_minus, controlunit_1_sp_plus_plus, controlunit_1_zfld,
       zeroflag_1_zf_out;
  wire [1:0] controlunit_1_armux;
  wire [2:0] controlunit_1_mux, ir_1_dst_2_0, ir_1_src_5_3, ir_1_src_8_6;
  wire [5:0] ir_1_alu_select_11_6;
  wire [11:0] adder_1_out, ir_1_output_12bit, multiplexer_1_out, multiplexer_5_out, pc_1_pc_out12,
       regbank_1_reg7sp;
  wire [15:0] alu_1_alu_output, multiplexer_3_out, regbank_1_reg0, regbank_1_reg1, regbank_1_reg2,
       regbank_1_reg3, regbank_1_reg4, regbank_1_reg5, regbank_1_reg6;
  wire [15:4] undriven;
  wire [15:12] multiplexer_5_out_2, regbank_1_reg7sp_2;

  Multiplexer #(.width(12), .enable("false")) multiplexer_1 (
    .in0(adder_1_out), .in1(mem_out[11:0]), .out(multiplexer_1_out), .sel(controlunit_1_retmux));
  Adder #(.width(12)) adder_1 (.a(ir_1_output_12bit), .b(undriven), .out(adder_1_out));  // open: cin, cout
  PC pc_1 (
    .pc_in12(multiplexer_1_out), .pc_inc(controlunit_1_pc_plus_plus), .pc_ld(controlunit_1_pcld),
    .clock(CLOCK), .pc_out12(pc_1_pc_out12));
  Multiplexer #(.select(2), .width(12), .enable("false")) multiplexer_2 (
    .in0(pc_1_pc_out12), .in1(multiplexer_5_out), .in2(regbank_1_reg7sp), .out(mem_address),
    .sel(controlunit_1_armux));  // open: in3
  RegBank regbank_1 (
    .data_in(mem_datain), .reg_sel(ir_1_dst_2_0), .regld(controlunit_1_regld),
    .sp_plus_plus(controlunit_1_sp_plus_plus), .sp_minus_minus(controlunit_1_sp_minus_minus), .clock(CLOCK),
    .Reg0(regbank_1_reg0), .Reg1(regbank_1_reg1), .Reg2(regbank_1_reg2), .Reg3(regbank_1_reg3),
    .Reg4(regbank_1_reg4), .Reg5(regbank_1_reg5), .Reg6(regbank_1_reg6),
    .Reg7sp({regbank_1_reg7sp_2, regbank_1_reg7sp}));
  Multiplexer #(.select(3), .width(16), .enable("false")) multiplexer_3 (
    .in0(regbank_1_reg0), .in1(regbank_1_reg1), .in2(regbank_1_reg2), .in3(regbank_1_reg3),
    .in4(regbank_1_reg4), .in5(regbank_1_reg5), .in6(regbank_1_reg6),
    .in7({regbank_1_reg7sp_2, regbank_1_reg7sp}), .out(multiplexer_3_out), .sel(ir_1_src_8_6));
  ZeroFlag zeroflag_1 (.zf_in(alu_1_zf), .zfld(controlunit_1_zfld), .clock(CLOCK), .zf_out(zeroflag_1_zf_out));
  Multiplexer #(.select(3), .width(16), .enable("false")) multiplexer_4 (
    .in0(mem_out), .in1(multiplexer_3_out), .in2({multiplexer_5_out_2, multiplexer_5_out}),
    .in3(alu_1_alu_output), .in4({undriven, 4'b0000}), .in5({16{1'b0}}), .in6({16{1'b0}}), .in7({16{1'b0}}),
    .out(mem_datain), .sel(controlunit_1_mux));
  ALU alu_1 (
    .ZF(alu_1_zf), .input1(multiplexer_3_out), .input2({multiplexer_5_out_2, multiplexer_5_out}),
    .alu_output(alu_1_alu_output), .alu_sel(ir_1_alu_select_11_6));
  Multiplexer #(.select(3), .width(16), .enable("false")) multiplexer_5 (
    .in0(regbank_1_reg0), .in1(regbank_1_reg1), .in2(regbank_1_reg2), .in3(regbank_1_reg3),
    .in4(regbank_1_reg4), .in5(regbank_1_reg5), .in6(regbank_1_reg6),
    .in7({regbank_1_reg7sp_2, regbank_1_reg7sp}), .out({multiplexer_5_out_2, multiplexer_5_out}),
    .sel(ir_1_src_5_3));
  ControlUnit controlunit_1 (
    .opcode(mem_out[15:12]), .clock(CLOCK), .zf(zeroflag_1_zf_out), .IRLD(controlunit_1_irld),
    .ZFLD(controlunit_1_zfld), .REGLD(controlunit_1_regld), .SP_plus_plus(controlunit_1_sp_plus_plus),
    .SP_minus_minus(controlunit_1_sp_minus_minus), .PC_plus_plus(controlunit_1_pc_plus_plus),
    .PCLD(controlunit_1_pcld), .ARMUX(controlunit_1_armux), .MUX(controlunit_1_mux),
    .RETMUX(controlunit_1_retmux), .MEMLD(mem_ld));  // open: FETCH
  IR ir_1 (
    .input_12bit(mem_out[11:0]), .LOAD(controlunit_1_irld), .CLK(CLOCK),
    .alu_select_11_6(ir_1_alu_select_11_6), .src_8_6(ir_1_src_8_6), .src_5_3(ir_1_src_5_3),
    .dst_2_0(ir_1_dst_2_0), .output_12bit(ir_1_output_12bit));
endmodule

module reg5bit (
  input  [4:0] input_5bit,
  input  clk,
  output [4:0] \output 
);

  wire not_1_out, not_2_out, not_3_out, not_4_out, not_5_out;

  S_R_Flip_Flop s_r_ff_1 (
    .S(input_5bit[0]), .clk(clk), .R(not_1_out), .Q(\output [0]), .en(1'b1));  // open: Qn, preset, reset
  not not_1 (not_1_out, input_5bit[0]);
  S_R_Flip_Flop s_r_ff_2 (
    .S(input_5bit[1]), .clk(clk), .R(not_2_out), .Q(\output [1]), .en(1'b1));  // open: Qn, preset, reset
  not not_2 (not_2_out, input_5bit[1]);
  S_R_Flip_Flop s_r_ff_3 (
    .S(input_5bit[2]), .clk(clk), .R(not_3_out), .Q(\output [2]), .en(1'b1));  // open: Qn, preset, reset
  not not_3 (not_3_out, input_5bit[2]);
  S_R_Flip_Flop s_r_ff_4 (
    .S(input_5bit[3]), .clk(clk), .R(not_4_out), .Q(\output [3]), .en(1'b1));  // open: Qn, preset, reset
  not not_4 (not_4_out, input_5bit[3]);
  S_R_Flip_Flop s_r_ff_5 (
    .S(input_5bit[4]), .clk(clk), .R(not_5_out), .Q(\output [4]), .en(1'b1));  // open: Qn, preset, reset
  not not_5 (not_5_out, input_5bit[4]);
endmodule
