// Logisim project ilk.circ as structural Verilog: 24 circuits, main circuit main
module main (
  input  clock
);

  wire cpu_1_mem_ld;
  wire [11:0] cpu_1_mem_address;
  wire [15:0] cpu_1_mem_datain, ram_1_data;

  CPU cpu_1 (
    .CLOCK(clock), .mem_out(ram_1_data), .mem_address(cpu_1_mem_address), .mem_datain(cpu_1_mem_datain),
    .mem_ld(cpu_1_mem_ld));
  RAM #(.addrWidth(12), .dataWidth(16), .bus("separate")) ram_1 (
    .addr(cpu_1_mem_address), .din(cpu_1_mem_datain), .data(ram_1_data), .str(cpu_1_mem_ld), .sel(1'b1),
    .clk(clock), .ld(1'b1), .clr(1'b0));

  // Notes on the sheet:
  //   MEMORY
endmodule

// reg
module reg16bit (
  input  clock,
  input  regld,
  input  [15:0] _16bit_input,
  output [15:0] _16bit_output
);

  wire not_1_out, not_2_out, not_3_out, not_4_out, not_5_out, not_6_out, not_7_out, not_8_out, not_9_out,
       not_10_out, not_11_out, not_12_out, not_13_out, not_14_out, not_15_out, not_16_out;

  not not_1 (not_1_out, _16bit_input[0]);
  not not_2 (not_2_out, _16bit_input[1]);
  not not_3 (not_3_out, _16bit_input[2]);
  not not_4 (not_4_out, _16bit_input[3]);
  not not_5 (not_5_out, _16bit_input[4]);
  not not_6 (not_6_out, _16bit_input[5]);
  not not_7 (not_7_out, _16bit_input[6]);
  not not_8 (not_8_out, _16bit_input[7]);
  not not_9 (not_9_out, _16bit_input[8]);
  not not_10 (not_10_out, _16bit_input[9]);
  not not_11 (not_11_out, _16bit_input[10]);
  not not_12 (not_12_out, _16bit_input[11]);
  not not_13 (not_13_out, _16bit_input[12]);
  not not_14 (not_14_out, _16bit_input[13]);
  not not_15 (not_15_out, _16bit_input[14]);
  not not_16 (not_16_out, _16bit_input[15]);
  S_R_Flip_Flop s_r_ff_1 (
    .S(_16bit_input[0]), .clk(clock), .R(not_1_out), .Q(_16bit_output[0]), .en(regld));  // open: Qn, preset, reset
  S_R_Flip_Flop s_r_ff_2 (
    .S(_16bit_input[1]), .clk(clock), .R(not_2_out), .Q(_16bit_output[1]), .en(regld));  // open: Qn, preset, reset
  S_R_Flip_Flop s_r_ff_3 (
    .S(_16bit_input[2]), .clk(clock), .R(not_3_out), .Q(_16bit_output[2]), .en(regld));  // open: Qn, preset, reset
  S_R_Flip_Flop s_r_ff_4 (
    .S(_16bit_input[3]), .clk(clock), .R(not_4_out), .Q(_16bit_output[3]), .en(regld));  // open: Qn, preset, reset
  S_R_Flip_Flop s_r_ff_5 (
    .S(_16bit_input[4]), .clk(clock), .R(not_5_out), .Q(_16bit_output[4]), .en(regld));  // open: Qn, preset, reset
  S_R_Flip_Flop s_r_ff_6 (
    .S(_16bit_input[5]), .clk(clock), .R(not_6_out), .Q(_16bit_output[5]), .en(regld));  // open: Qn, preset, reset
  S_R_Flip_Flop s_r_ff_7 (
    .S(_16bit_input[6]), .clk(clock), .R(not_7_out), .Q(_16bit_output[6]), .en(regld));  // open: Qn, preset, reset
  S_R_Flip_Flop s_r_ff_8 (
    .S(_16bit_input[7]), .clk(clock), .R(not_8_out), .Q(_16bit_output[7]), .en(regld));  // open: Qn, preset, reset
  S_R_Flip_Flop s_r_ff_9 (
    .S(_16bit_input[8]), .clk(clock), .R(not_9_out), .Q(_16bit_output[8]), .en(regld));  // open: Qn, preset, reset
  S_R_Flip_Flop s_r_ff_10 (
    .S(_16bit_input[9]), .clk(clock), .R(not_10_out), .Q(_16bit_output[9]), .en(regld));  // open: Qn, preset, reset
  S_R_Flip_Flop s_r_ff_11 (
    .S(_16bit_input[10]), .clk(clock), .R(not_11_out), .Q(_16bit_output[10]), .en(regld));  // open: Qn, preset, reset
  S_R_Flip_Flop s_r_ff_12 (
    .S(_16bit_input[11]), .clk(clock), .R(not_12_out), .Q(_16bit_output[11]), .en(regld));  // open: Qn, preset, reset
  S_R_Flip_Flop s_r_ff_13 (
    .S(_16bit_input[12]), .clk(clock), .R(not_13_out), .Q(_16bit_output[12]), .en(regld));  // open: Qn, preset, reset
  S_R_Flip_Flop s_r_ff_14 (
    .S(_16bit_input[13]), .clk(clock), .R(not_14_out), .Q(_16bit_output[13]), .en(regld));  // open: Qn, preset, reset
  S_R_Flip_Flop s_r_ff_15 (
    .S(_16bit_input[14]), .clk(clock), .R(not_15_out), .Q(_16bit_output[14]), .en(regld));  // open: Qn, preset, reset
  S_R_Flip_Flop s_r_ff_16 (
    .S(_16bit_input[15]), .clk(clock), .R(not_16_out), .Q(_16bit_output[15]), .en(regld));  // open: Qn, preset, reset
endmodule

module reg7SP (
  input  regld,
  input  inc,
  input  dec,
  input  clock,
  input  [15:0] _16bit_input_sp,
  output [15:0] _16bit_output_sp
);

  wire or_1_out;
  wire [15:0] adder_1_out, multiplexer_1_out, subtractor_1_out;

  Adder #(.width(16)) adder_1 (.a(_16bit_output_sp), .b(16'h1), .out(adder_1_out));  // open: cin, cout
  Subtractor #(.width(16)) subtractor_1 (.a(_16bit_output_sp), .b(16'h1), .out(subtractor_1_out));  // open: bin, bout
  Multiplexer #(.select(2), .width(16), .enable("false")) multiplexer_1 (
    .in0(_16bit_input_sp), .in1(adder_1_out), .in2(subtractor_1_out), .in3({16{1'b0}}),
    .out(multiplexer_1_out), .sel({dec, inc}));
  or or_1 (or_1_out, dec, inc, regld);
  reg16bit reg16bit_1 (
    .regld(or_1_out), ._16bit_input(multiplexer_1_out), .clock(clock), ._16bit_output(_16bit_output_sp));
endmodule

module RegBank (
  input  clock,
  input  [15:0] data_in,
  input  [2:0] reg_sel,
  input  regld,
  input  sp_plus_plus,
  input  sp_minus_minus,
  output [15:0] Reg0,
  output [15:0] Reg1,
  output [15:0] Reg2,
  output [15:0] Reg3,
  output [15:0] Reg4,
  output [15:0] Reg5,
  output [15:0] Reg6,
  output [15:0] Reg7sp
);

  wire and_1_out, and_2_out, and_3_out, and_4_out, and_5_out, and_6_out, and_7_out, and_8_out,
       decoder_1_out0, decoder_1_out1, decoder_1_out2, decoder_1_out3, decoder_1_out4, decoder_1_out5,
       decoder_1_out6, decoder_1_out7, or_1_out, or_2_out;

  Decoder #(.select(3), .enable("false")) decoder_1 (
    .out0(decoder_1_out0), .out1(decoder_1_out1), .out2(decoder_1_out2), .out3(decoder_1_out3),
    .out4(decoder_1_out4), .out5(decoder_1_out5), .out6(decoder_1_out6), .out7(decoder_1_out7), .sel(reg_sel));
  and and_1 (and_1_out, decoder_1_out0, regld);
  and and_2 (and_2_out, decoder_1_out1, regld);
  and and_3 (and_3_out, decoder_1_out2, regld);
  and and_4 (and_4_out, decoder_1_out3, regld);
  and and_5 (and_5_out, decoder_1_out4, regld);
  and and_6 (and_6_out, decoder_1_out5, regld);
  and and_7 (and_7_out, decoder_1_out6, regld);
  and and_8 (and_8_out, decoder_1_out7, regld);
  or or_1 (or_1_out, sp_plus_plus, sp_minus_minus);
  or or_2 (or_2_out, and_8_out, or_1_out);
  reg16bit reg16bit_1 (.regld(and_1_out), ._16bit_input(data_in), .clock(clock), ._16bit_output(Reg0));
  reg16bit reg16bit_2 (.regld(and_2_out), ._16bit_input(data_in), .clock(clock), ._16bit_output(Reg1));
  reg16bit reg16bit_3 (.regld(and_3_out), ._16bit_input(data_in), .clock(clock), ._16bit_output(Reg2));
  reg16bit reg16bit_4 (.regld(and_4_out), ._16bit_input(data_in), .clock(clock), ._16bit_output(Reg3));
  reg16bit reg16bit_5 (.regld(and_5_out), ._16bit_input(data_in), .clock(clock), ._16bit_output(Reg4));
  reg16bit reg16bit_6 (.regld(and_6_out), ._16bit_input(data_in), .clock(clock), ._16bit_output(Reg5));
  reg16bit reg16bit_7 (.regld(and_7_out), ._16bit_input(data_in), .clock(clock), ._16bit_output(Reg6));
  reg7SP reg7sp_1 (
    .regld(or_2_out), .inc(sp_plus_plus), .dec(sp_minus_minus), ._16bit_input_sp(data_in), .clock(clock),
    ._16bit_output_sp(Reg7sp));
endmodule

module reg12bit (
  input  CLK,
  input  [11:0] input_12bit,
  input  LOAD,
  output [11:0] output_12bit
);

  wire not_1_out, not_2_out, not_3_out, not_4_out, not_5_out, not_6_out, not_7_out, not_8_out, not_9_out,
       not_10_out, not_11_out, not_12_out;

  not not_1 (not_1_out, input_12bit[0]);
  not not_2 (not_2_out, input_12bit[1]);
  not not_3 (not_3_out, input_12bit[2]);
  not not_4 (not_4_out, input_12bit[3]);
  not not_5 (not_5_out, input_12bit[4]);
  not not_6 (not_6_out, input_12bit[5]);
  not not_7 (not_7_out, input_12bit[6]);
  not not_8 (not_8_out, input_12bit[7]);
  not not_9 (not_9_out, input_12bit[8]);
  not not_10 (not_10_out, input_12bit[9]);
  not not_11 (not_11_out, input_12bit[10]);
  not not_12 (not_12_out, input_12bit[11]);
  S_R_Flip_Flop s_r_ff_1 (
    .S(input_12bit[0]), .clk(CLK), .R(not_1_out), .Q(output_12bit[0]), .en(LOAD));  // open: Qn, preset, reset
  S_R_Flip_Flop s_r_ff_2 (
    .S(input_12bit[1]), .clk(CLK), .R(not_2_out), .Q(output_12bit[1]), .en(LOAD));  // open: Qn, preset, reset
  S_R_Flip_Flop s_r_ff_3 (
    .S(input_12bit[2]), .clk(CLK), .R(not_3_out), .Q(output_12bit[2]), .en(LOAD));  // open: Qn, preset, reset
  S_R_Flip_Flop s_r_ff_4 (
    .S(input_12bit[3]), .clk(CLK), .R(not_4_out), .Q(output_12bit[3]), .en(LOAD));  // open: Qn, preset, reset
  S_R_Flip_Flop s_r_ff_5 (
    .S(input_12bit[4]), .clk(CLK), .R(not_5_out), .Q(output_12bit[4]), .en(LOAD));  // open: Qn, preset, reset
  S_R_Flip_Flop s_r_ff_6 (
    .S(input_12bit[5]), .clk(CLK), .R(not_6_out), .Q(output_12bit[5]), .en(LOAD));  // open: Qn, preset, reset
  S_R_Flip_Flop s_r_ff_7 (
    .S(input_12bit[6]), .clk(CLK), .R(not_7_out), .Q(output_12bit[6]), .en(LOAD));  // open: Qn, preset, reset
  S_R_Flip_Flop s_r_ff_8 (
    .S(input_12bit[7]), .clk(CLK), .R(not_8_out), .Q(output_12bit[7]), .en(LOAD));  // open: Qn, preset, reset
  S_R_Flip_Flop s_r_ff_9 (
    .S(input_12bit[8]), .clk(CLK), .R(not_9_out), .Q(output_12bit[8]), .en(LOAD));  // open: Qn, preset, reset
  S_R_Flip_Flop s_r_ff_10 (
    .S(input_12bit[9]), .clk(CLK), .R(not_10_out), .Q(output_12bit[9]), .en(LOAD));  // open: Qn, preset, reset
  S_R_Flip_Flop s_r_ff_11 (
    .S(input_12bit[10]), .clk(CLK), .R(not_11_out), .Q(output_12bit[10]), .en(LOAD));  // open: Qn, preset, reset
  S_R_Flip_Flop s_r_ff_12 (
    .S(input_12bit[11]), .clk(CLK), .R(not_12_out), .Q(output_12bit[11]), .en(LOAD));  // open: Qn, preset, reset
endmodule

module IR (
  input  CLK,
  input  [11:0] input_12bit,
  input  IRLD,
  output [5:0] alu_select_11_6,
  output [2:0] src_8_6,
  output [2:0] src_5_3,
  output [2:0] dst_2_0,
  output [11:0] output_12bit
);

  wire not_1_out, not_2_out, not_3_out, not_4_out, not_5_out, not_6_out, not_7_out, not_8_out, not_9_out,
       not_10_out, not_11_out, not_12_out;

  not not_1 (not_1_out, input_12bit[0]);
  not not_2 (not_2_out, input_12bit[1]);
  not not_3 (not_3_out, input_12bit[2]);
  not not_4 (not_4_out, input_12bit[3]);
  not not_5 (not_5_out, input_12bit[4]);
  not not_6 (not_6_out, input_12bit[5]);
  not not_7 (not_7_out, input_12bit[6]);
  not not_8 (not_8_out, input_12bit[7]);
  not not_9 (not_9_out, input_12bit[8]);
  not not_10 (not_10_out, input_12bit[9]);
  not not_11 (not_11_out, input_12bit[10]);
  not not_12 (not_12_out, input_12bit[11]);
  S_R_Flip_Flop s_r_ff_1 (
    .S(input_12bit[0]), .clk(CLK), .R(not_1_out), .Q(dst_2_0[0]), .en(IRLD));  // open: Qn, preset, reset
  S_R_Flip_Flop s_r_ff_2 (
    .S(input_12bit[1]), .clk(CLK), .R(not_2_out), .Q(dst_2_0[1]), .en(IRLD));  // open: Qn, preset, reset
  S_R_Flip_Flop s_r_ff_3 (
    .S(input_12bit[2]), .clk(CLK), .R(not_3_out), .Q(dst_2_0[2]), .en(IRLD));  // open: Qn, preset, reset
  S_R_Flip_Flop s_r_ff_4 (
    .S(input_12bit[3]), .clk(CLK), .R(not_4_out), .Q(output_12bit[3]), .en(IRLD));  // open: Qn, preset, reset
  S_R_Flip_Flop s_r_ff_5 (
    .S(input_12bit[4]), .clk(CLK), .R(not_5_out), .Q(output_12bit[4]), .en(IRLD));  // open: Qn, preset, reset
  S_R_Flip_Flop s_r_ff_6 (
    .S(input_12bit[5]), .clk(CLK), .R(not_6_out), .Q(output_12bit[5]), .en(IRLD));  // open: Qn, preset, reset
  S_R_Flip_Flop s_r_ff_7 (
    .S(input_12bit[6]), .clk(CLK), .R(not_7_out), .Q(alu_select_11_6[0]), .en(IRLD));  // open: Qn, preset, reset
  S_R_Flip_Flop s_r_ff_8 (
    .S(input_12bit[7]), .clk(CLK), .R(not_8_out), .Q(alu_select_11_6[1]), .en(IRLD));  // open: Qn, preset, reset
  S_R_Flip_Flop s_r_ff_9 (
    .S(input_12bit[8]), .clk(CLK), .R(not_9_out), .Q(alu_select_11_6[2]), .en(IRLD));  // open: Qn, preset, reset
  S_R_Flip_Flop s_r_ff_10 (
    .S(input_12bit[9]), .clk(CLK), .R(not_10_out), .Q(alu_select_11_6[3]), .en(IRLD));  // open: Qn, preset, reset
  S_R_Flip_Flop s_r_ff_11 (
    .S(input_12bit[10]), .clk(CLK), .R(not_11_out), .Q(alu_select_11_6[4]), .en(IRLD));  // open: Qn, preset, reset
  S_R_Flip_Flop s_r_ff_12 (
    .S(input_12bit[11]), .clk(CLK), .R(not_12_out), .Q(alu_select_11_6[5]), .en(IRLD));  // open: Qn, preset, reset

  assign {output_12bit[11:6], output_12bit[2:0]} = {alu_select_11_6, dst_2_0};
  assign src_5_3 = output_12bit[5:3];
  assign src_8_6 = alu_select_11_6[2:0];
endmodule

module PC (
  input  clock,
  input  [11:0] pc_in12,
  input  pc_inc,
  input  pc_ld,
  output [11:0] pc_out12
);

  wire or_1_out;
  wire [11:0] adder_1_out, multiplexer_1_out;

  Adder #(.width(12)) adder_1 (.a(pc_out12), .b(12'h1), .out(adder_1_out));  // open: cin, cout
  Multiplexer #(.width(12), .enable("false")) multiplexer_1 (
    .in0(pc_in12), .in1(adder_1_out), .out(multiplexer_1_out), .sel(pc_inc));
  or or_1 (or_1_out, pc_inc, pc_ld);
  reg12bit reg12bit_1 (.input_12bit(multiplexer_1_out), .LOAD(or_1_out), .CLK(clock), .output_12bit(pc_out12));
endmodule

// ZF
module ZeroFlag (
  input  clock,
  input  zf_in,
  input  zfld,
  output zf_out
);

  wire not_1_out;

  not not_1 (not_1_out, zf_in);
  S_R_Flip_Flop s_r_ff_1 (.S(zf_in), .clk(clock), .R(not_1_out), .Q(zf_out), .en(zfld));  // open: Qn, preset, reset
endmodule

module ALU (
  input  [15:0] input1,
  input  [15:0] input2,
  input  [5:0] alu_sel,
  output [15:0] alu_output,
  output ZeroFlag_forREG
);

  wire and_1_out;
  wire [15:0] adder_1_out, adder_2_out, and_2_out, multiplexer_1_out, multiplexer_3_out, not_1_out, or_1_out,
       subtractor_1_out, subtractor_2_out, xor_1_out;

  Adder #(.width(16)) adder_1 (.a(input1), .b(input2), .out(adder_1_out));  // open: cin, cout
  Subtractor #(.width(16)) subtractor_1 (.a(input1), .b(input1), .out(subtractor_1_out));  // open: bin, bout
  Multiplexer #(.select(3), .width(16), .enable("false")) multiplexer_1 (
    .in0(adder_1_out), .in1(subtractor_1_out), .in2(and_2_out), .in3(or_1_out), .in4(xor_1_out),
    .in5({16{1'b0}}), .in6({16{1'b0}}), .in7({16{1'b0}}), .out(multiplexer_1_out), .sel(alu_sel[5:3]));
  and and_1 (and_1_out, alu_sel[5], alu_sel[4], alu_sel[3]);
  assign and_2_out = input1 & input1;  // AND_Gate and_2, 16 bits wide
  Multiplexer #(.width(16), .enable("false")) multiplexer_2 (
    .in0(multiplexer_1_out), .in1(multiplexer_3_out), .out(alu_output), .sel(and_1_out));
  assign or_1_out = input1 | input1;  // OR_Gate or_1, 16 bits wide
  assign xor_1_out = input1 ^ input1;  // XOR_Gate xor_1, 16 bits wide
  assign not_1_out = ~input2;  // NOT_Gate not_1, 16 bits wide
  Multiplexer #(.select(3), .width(16), .enable("false")) multiplexer_3 (
    .in0(not_1_out), .in1(input2), .in2(adder_2_out), .in3(subtractor_2_out), .in4({16{1'b0}}),
    .in5({16{1'b0}}), .in6({16{1'b0}}), .in7({16{1'b0}}), .out(multiplexer_3_out), .sel(alu_sel[2:0]));
  Adder #(.width(16)) adder_2 (.a(input2), .b(16'h1), .out(adder_2_out));  // open: cin, cout
  nor nor_1 (ZeroFlag_forREG, alu_output[0], alu_output[1], alu_output[2], alu_output[3], alu_output[4], alu_output[5], alu_output[6], alu_output[7], alu_output[8], alu_output[9], alu_output[10], alu_output[11], alu_output[12], alu_output[13], alu_output[14], alu_output[15]);
  Subtractor #(.width(16)) subtractor_2 (.a(input2), .b(16'h1), .out(subtractor_2_out));  // open: bin, bout
endmodule

module reg4bit (
  input  [3:0] input_4bit,
  input  clk,
  output [3:0] \output 
);

  wire not_1_out, not_2_out, not_3_out, not_4_out;

  S_R_Flip_Flop s_r_ff_1 (
    .S(input_4bit[0]), .clk(clk), .R(not_1_out), .Q(\output [0]), .en(1'b1));  // open: Qn, preset, reset
  not not_1 (not_1_out, input_4bit[0]);
  S_R_Flip_Flop s_r_ff_2 (
    .S(input_4bit[1]), .clk(clk), .R(not_2_out), .Q(\output [1]), .en(1'b1));  // open: Qn, preset, reset
  not not_2 (not_2_out, input_4bit[1]);
  S_R_Flip_Flop s_r_ff_3 (
    .S(input_4bit[2]), .clk(clk), .R(not_3_out), .Q(\output [2]), .en(1'b1));  // open: Qn, preset, reset
  not not_3 (not_3_out, input_4bit[2]);
  S_R_Flip_Flop s_r_ff_4 (
    .S(input_4bit[3]), .clk(clk), .R(not_4_out), .Q(\output [3]), .en(1'b1));  // open: Qn, preset, reset
  not not_4 (not_4_out, input_4bit[3]);
endmodule

// CU
module ControlUnit (
  input  [3:0] opcode,
  input  zf,
  input  clock,
  output IRLD,
  output ZFLD,
  output REGLD,
  output SP_plus_plus,
  output SP_minus_minus,
  output PC_plus_plus,
  output PCLD,
  output [1:0] ARMUX,
  output [2:0] MUX,
  output RETMUX,
  output MEMLD,
  output FETCH
);

  wire not_1_out, not_2_out, not_3_out;
  wire [1:1] and_1_out;
  wire [4:0] multiplexer_1_out, multiplexer_2_out, reg5bit_1_output, rom_1_data;

  not not_1 (not_1_out, opcode[3]);
  not not_2 (not_2_out, opcode[1]);
  and and_1 (and_1_out[1], not_1_out, opcode[2], not_2_out, not_3_out);
  not not_3 (not_3_out, opcode[0]);
  Multiplexer #(.select(2), .width(5), .enable("false")) multiplexer_1 (
    .in0({opcode, 1'b0}), .in1({opcode, 1'b0}), .in2({5{1'b0}}), .in3(5'b01010), .out(multiplexer_1_out),
    .sel({and_1_out[1], zf}));
  Multiplexer #(.width(5), .enable("false")) multiplexer_2 (
    .in0(rom_1_data), .in1(multiplexer_1_out), .out(multiplexer_2_out), .sel(FETCH));
  reg5bit reg5bit_1 (.input_5bit(multiplexer_2_out), .clk(clock), .\output (reg5bit_1_output));
  ROM #(.addrWidth(5), .dataWidth(20)) rom_1 (
    .addr(reg5bit_1_output),
    .data({FETCH, MEMLD, RETMUX, MUX[0], MUX[1], MUX[2], ARMUX[0], ARMUX[1], PCLD, PC_plus_plus, SP_minus_minus, SP_plus_plus, REGLD, ZFLD, IRLD, rom_1_data}));  // open: sel

  // Notes on the sheet:
  //   isJmp
  //   0 0101(jmp)
  //   contents of rom_1 (hex, n*v repeats v):
  //   80420 480 2080 52000 0 800 0 18080 51200 10c 45a00 10d 1080 21800
endmodule

module CPU (
  input  CLOCK,
  input  [15:0] mem_out,
  output [11:0] mem_address,
  output [15:0] mem_datain,
  output mem_ld
);

  wire alu_1_zeroflag_forreg, controlunit_1_irld, controlunit_1_pc_plus_plus, controlunit_1_pcld,
       controlunit_1_regld, controlunit_1_retmux, controlunit_1_sp_minus_minus, controlunit_1_sp_plus_plus,
       controlunit_1_zfld, zeroflag_1_zf_out;
  wire [1:0] controlunit_1_armux;
  wire [2:0] controlunit_1_mux, ir_1_dst_2_0, ir_1_src_5_3, ir_1_src_8_6;
  wire [5:0] ir_1_alu_select_11_6;
  wire [11:0] adder_1_out, ir_1_output_12bit, multiplexer_1_out, multiplexer_5_out, pc_1_pc_out12,
       regbank_1_reg7sp;
  wire [15:0] alu_1_alu_output, multiplexer_3_out, regbank_1_reg0, regbank_1_reg1, regbank_1_reg2,
       regbank_1_reg3, regbank_1_reg4, regbank_1_reg5, regbank_1_reg6;
  wire [15:4] undriven;
  wire [15:12] multiplexer_5_out_2, regbank_1_reg7sp_2;

  Multiplexer #(.width(12), .enable("false")) multiplexer_1 (
    .in0(adder_1_out), .in1(mem_out[11:0]), .out(multiplexer_1_out), .sel(controlunit_1_retmux));
  Adder #(.width(12)) adder_1 (.a(ir_1_output_12bit), .b(undriven), .out(adder_1_out));  // open: cin, cout
  PC pc_1 (
    .pc_in12(multiplexer_1_out), .pc_inc(controlunit_1_pc_plus_plus), .pc_ld(controlunit_1_pcld),
    .clock(CLOCK), .pc_out12(pc_1_pc_out12));
  Multiplexer #(.select(2), .width(12), .enable("false")) multiplexer_2 (
    .in0(pc_1_pc_out12), .in1(multiplexer_5_out), .in2(regbank_1_reg7sp), .out(mem_address),
    .sel(controlunit_1_armux));  // open: in3
  RegBank regbank_1 (
    .data_in(mem_datain), .reg_sel(ir_1_dst_2_0), .regld(controlunit_1_regld),
    .sp_plus_plus(controlunit_1_sp_plus_plus), .sp_minus_minus(controlunit_1_sp_minus_minus), .clock(CLOCK),
    .Reg0(regbank_1_reg0), .Reg1(regbank_1_reg1), .Reg2(regbank_1_reg2), .Reg3(regbank_1_reg3),
    .Reg4(regbank_1_reg4), .Reg5(regbank_1_reg5), .Reg6(regbank_1_reg6),
    .Reg7sp({regbank_1_reg7sp_2, regbank_1_reg7sp}));
  Multiplexer #(.select(3), .width(16), .enable("false")) multiplexer_3 (
    .in0(regbank_1_reg0), .in1(regbank_1_reg1), .in2(regbank_1_reg2), .in3(regbank_1_reg3),
    .in4(regbank_1_reg4), .in5(regbank_1_reg5), .in6(regbank_1_reg6),
    .in7({regbank_1_reg7sp_2, regbank_1_reg7sp}), .out(multiplexer_3_out), .sel(ir_1_src_8_6));
  ZeroFlag zeroflag_1 (
    .zf_in(alu_1_zeroflag_forreg), .zfld(controlunit_1_zfld), .clock(CLOCK), .zf_out(zeroflag_1_zf_out));
  Multiplexer #(.select(3), .width(16), .enable("false")) multiplexer_4 (
    .in0(mem_out), .in1(multiplexer_3_out), .in2({multiplexer_5_out_2, multiplexer_5_out}),
    .in3(alu_1_alu_output), .in4({undriven, 4'b0000}), .in5({16{1'b0}}), .in6({16{1'b0}}), .in7({16{1'b0}}),
    .out(mem_datain), .sel(controlunit_1_mux));
  ALU alu_1 (
    .ZeroFlag_forREG(alu_1_zeroflag_forreg), .input1(multiplexer_3_out),
    .input2({multiplexer_5_out_2, multiplexer_5_out}), .alu_output(alu_1_alu_output),
    .alu_sel(ir_1_alu_select_11_6));
  Multiplexer #(.select(3), .width(16), .enable("false")) multiplexer_5 (
    .in0(regbank_1_reg0), .in1(regbank_1_reg1), .in2(regbank_1_reg2), .in3(regbank_1_reg3),
    .in4(regbank_1_reg4), .in5(regbank_1_reg5), .in6(regbank_1_reg6),
    .in7({regbank_1_reg7sp_2, regbank_1_reg7sp}), .out({multiplexer_5_out_2, multiplexer_5_out}),
    .sel(ir_1_src_5_3));
  ControlUnit controlunit_1 (
    .opcode(mem_out[15:12]), .clock(CLOCK), .zf(zeroflag_1_zf_out), .IRLD(controlunit_1_irld),
    .ZFLD(controlunit_1_zfld), .REGLD(controlunit_1_regld), .SP_plus_plus(controlunit_1_sp_plus_plus),
    .SP_minus_minus(controlunit_1_sp_minus_minus), .PC_plus_plus(controlunit_1_pc_plus_plus),
    .PCLD(controlunit_1_pcld), .ARMUX(controlunit_1_armux), .MUX(controlunit_1_mux),
    .RETMUX(controlunit_1_retmux), .MEMLD(mem_ld));  // open: FETCH
  IR ir_1 (
    .input_12bit(mem_out[11:0]), .IRLD(controlunit_1_irld), .CLK(CLOCK),
    .alu_select_11_6(ir_1_alu_select_11_6), .src_8_6(ir_1_src_8_6), .src_5_3(ir_1_src_5_3),
    .dst_2_0(ir_1_dst_2_0), .output_12bit(ir_1_output_12bit));
endmodule

module reg5bit (
  input  [4:0] input_5bit,
  input  clk,
  output [4:0] \output 
);

  wire not_1_out, not_2_out, not_3_out, not_4_out, not_5_out;

  S_R_Flip_Flop s_r_ff_1 (
    .S(input_5bit[0]), .clk(clk), .R(not_1_out), .Q(\output [0]), .en(1'b1));  // open: Qn, preset, reset
  not not_1 (not_1_out, input_5bit[0]);
  S_R_Flip_Flop s_r_ff_2 (
    .S(input_5bit[1]), .clk(clk), .R(not_2_out), .Q(\output [1]), .en(1'b1));  // open: Qn, preset, reset
  not not_2 (not_2_out, input_5bit[1]);
  S_R_Flip_Flop s_r_ff_3 (
    .S(input_5bit[2]), .clk(clk), .R(not_3_out), .Q(\output [2]), .en(1'b1));  // open: Qn, preset, reset
  not not_3 (not_3_out, input_5bit[2]);
  S_R_Flip_Flop s_r_ff_4 (
    .S(input_5bit[3]), .clk(clk), .R(not_4_out), .Q(\output [3]), .en(1'b1));  // open: Qn, preset, reset
  not not_4 (not_4_out, input_5bit[3]);
  S_R_Flip_Flop s_r_ff_5 (
    .S(input_5bit[4]), .clk(clk), .R(not_5_out), .Q(\output [4]), .en(1'b1));  // open: Qn, preset, reset
  not not_5 (not_5_out, input_5bit[4]);
endmodule

module RegBankINT (
  input  clock,
  input  [15:0] data_in,
  input  [2:0] reg_sel,
  input  CLI,
  input  FLAGLD,
  input  STI,
  input  ZFLD,
  input  ZFlag_from_alu,
  input  regld,
  input  sp_plus_plus,
  input  sp_minus_minus,
  output [15:0] Reg0,
  output [15:0] Reg1,
  output [15:0] Reg2,
  output IF,
  output ZF,
  output [15:0] Reg3,
  output [15:0] Reg4,
  output [15:0] Reg5,
  output [15:0] Reg6,
  output [15:0] Reg7sp
);

  wire and_1_out, and_2_out, and_3_out, and_4_out, and_5_out, and_6_out, and_7_out, and_8_out,
       decoder_1_out0, decoder_1_out1, decoder_1_out2, decoder_1_out3, decoder_1_out4, decoder_1_out5,
       decoder_1_out6, decoder_1_out7, or_1_out, or_2_out;
  wire [15:0] reg16bit_7__16bit_output;

  Decoder #(.select(3), .enable("false")) decoder_1 (
    .out0(decoder_1_out0), .out1(decoder_1_out1), .out2(decoder_1_out2), .out3(decoder_1_out3),
    .out4(decoder_1_out4), .out5(decoder_1_out5), .out6(decoder_1_out6), .out7(decoder_1_out7), .sel(reg_sel));
  and and_1 (and_1_out, decoder_1_out0, regld);
  and and_2 (and_2_out, decoder_1_out1, regld);
  and and_3 (and_3_out, decoder_1_out2, regld);
  and and_4 (and_4_out, decoder_1_out3, regld);
  and and_5 (and_5_out, decoder_1_out4, regld);
  and and_6 (and_6_out, decoder_1_out5, regld);
  and and_7 (and_7_out, decoder_1_out6, regld);
  and and_8 (and_8_out, decoder_1_out7, regld);
  or or_1 (or_1_out, sp_plus_plus, sp_minus_minus);
  or or_2 (or_2_out, and_8_out, or_1_out);
  reg16bit reg16bit_1 (.regld(and_1_out), ._16bit_input(data_in), .clock(clock), ._16bit_output(Reg0));
  reg16bit reg16bit_2 (.regld(and_2_out), ._16bit_input(data_in), .clock(clock), ._16bit_output(Reg1));
  reg16bit reg16bit_3 (.regld(and_3_out), ._16bit_input(data_in), .clock(clock), ._16bit_output(Reg2));
  reg16bit reg16bit_4 (.regld(and_4_out), ._16bit_input(data_in), .clock(clock), ._16bit_output(Reg3));
  reg16bit reg16bit_5 (.regld(and_5_out), ._16bit_input(data_in), .clock(clock), ._16bit_output(Reg4));
  reg16bit reg16bit_6 (.regld(and_6_out), ._16bit_input(data_in), .clock(clock), ._16bit_output(Reg5));
  reg16bit reg16bit_7 (
    .regld(and_7_out), ._16bit_input(data_in), .clock(clock), ._16bit_output(reg16bit_7__16bit_output));
  reg7SP reg7sp_1 (
    .regld(or_2_out), .inc(sp_plus_plus), .dec(sp_minus_minus), ._16bit_input_sp(data_in), .clock(clock),
    ._16bit_output_sp(Reg7sp));
  flag flag_1 (
    .datain(reg16bit_7__16bit_output[1:0]), .FLAGLD(FLAGLD), .CLI(CLI), .Clock(clock), .STI(STI),
    .ZFLD(ZFLD), .ZeroFlagFromAlu(ZFlag_from_alu), .dataOut({IF, Reg6[0]}));

  assign Reg6[15:1] = {{14{1'b0}}, IF};
  assign ZF = Reg6[0];
endmodule

module PIC (
  input  IN1,
  input  IN2,
  output INT,
  output [15:0] dataOut
);

  wire priority_encoder_1_en_out;

  Priority_Encoder priority_encoder_1 (
    .in0(1'b0), .in1(1'b0), .in2(IN1), .in3(1'b0), .in4(1'b0), .in5(IN2), .in6(1'b0), .in7(1'b0),
    .out(dataOut[2:0]), .en_out(priority_encoder_1_en_out));  // open: en_in, gs
  not not_1 (INT, priority_encoder_1_en_out);

  assign dataOut[15:3] = {13{1'b0}};
endmodule

// kpad
module keypad (
  input  [15:0] keypad_in,
  input  readyButton,
  input  CS,
  input  A0,
  output [15:0] keypad_out,
  output keypadINT
);

  wire and_1_out;
  wire [15:0] dataReg_q, statusReg_q;

  S_R_Flip_Flop s_r_ff_1 (
    .S(1'b1), .clk(readyButton), .R(1'b0), .Q(keypadINT), .preset(1'b0), .reset(and_1_out), .en(1'b1));  // open: Qn
  Register #(.width(16)) dataReg (.D(keypad_in), .en(1'b1), .Q(dataReg_q), .clk(keypadINT));  // open: clr
  Register #(.width(16)) statusReg (.D(16'h1), .en(1'b1), .Q(statusReg_q), .clk(keypadINT), .clr(and_1_out));
  and and_1 (and_1_out, CS, ~A0);  // AND_Gate
  Multiplexer #(.width(16), .enable("false")) multiplexer_1 (
    .in0(dataReg_q), .in1(statusReg_q), .out(keypad_out), .sel(A0));
endmodule

// CU
module interrupt_cu (
  input  [3:0] opcode,
  input  zf_fromReg,
  input  IF_INT,
  input  clock,
  output [4:0] nextaddress,
  output MEMLD,
  output INTACK,
  output [1:0] ARMUX,
  output PCLD,
  output PC_plus_plus,
  output RETMUX,
  output SP_plus_plus,
  output SP_minus_minus,
  output FLAGLD,
  output CLI,
  output STI,
  output REGLD,
  output ZFLD,
  output [2:0] MUX,
  output IRLD,
  output INT_LD,
  output FETCH
);

  wire and_1_out, and_2_out, not_1_out, not_2_out, not_3_out;
  wire [1:1] and_3_out;
  wire [4:0] multiplexer_1_out, multiplexer_2_out, multiplexer_3_out, reg5bit_1_output;

  and and_1 (and_1_out, ~nextaddress[0], ~nextaddress[1], ~nextaddress[2], ~nextaddress[3], ~nextaddress[4]);  // AND_Gate
  not not_1 (not_1_out, opcode[3]);
  and and_2 (and_2_out, IF_INT, and_1_out);
  not not_2 (not_2_out, opcode[0]);
  not not_3 (not_3_out, opcode[1]);
  and and_3 (and_3_out[1], not_1_out, opcode[2], not_3_out, not_2_out);
  Multiplexer #(.select(2), .width(5), .enable("false")) multiplexer_1 (
    .in0({1'b0, opcode}), .in1({1'b0, opcode}), .in2({1'b0, opcode}), .in3(5'b00101),
    .out(multiplexer_1_out), .sel({and_3_out[1], zf_fromReg}));
  Multiplexer #(.width(5), .enable("false")) multiplexer_2 (
    .in0(multiplexer_1_out), .in1(5'b10011), .out(multiplexer_2_out), .sel(and_2_out));
  Multiplexer #(.width(5), .enable("false")) multiplexer_3 (
    .in0(nextaddress), .in1(multiplexer_2_out), .out(multiplexer_3_out), .sel(FETCH));
  reg5bit reg5bit_1 (.input_5bit(multiplexer_3_out), .clk(clock), .\output (reg5bit_1_output));
  ROM #(.addrWidth(5), .dataWidth(25)) rom_1 (
    .addr(reg5bit_1_output),
    .data({FETCH, INT_LD, IRLD, MUX, ZFLD, REGLD, STI, CLI, FLAGLD, SP_minus_minus, SP_plus_plus, RETMUX, PC_plus_plus, PCLD, ARMUX, INTACK, MEMLD, nextaddress}));  // open: sel

  // Notes on the sheet:
  //   isJmp
  //   contents of rom_1 (hex, n*v repeats v):
  //   1400400 20400 20080 800a0 0 200 0 1e0000 82120 100f 202320 1010 10000 8000 1011 20100 b00 1b12 4113
  //   28a134 a02175 b80
endmodule

// CPU
module interruptCPU (
  input  CLOCK,
  input  [15:0] mem_out,
  input  INT,
  output MEMLD,
  output INTACK,
  output [11:0] mem_address,
  output [15:0] mem_datain,
  output INTLD
);

  wire alu_1_zeroflag_forreg, and_1_out, CLI, FLAGLD, IRLD, PC_plus_plus, PCLD, regbankint_1_if,
       regbankint_1_zf, REGLD, RETMUX, SP_minus_minus, SP_plus_plus, STI, ZFLD;
  wire [1:0] ARMUX;
  wire [2:0] ir_1_dst_2_0, ir_1_src_5_3, ir_1_src_8_6, MUX;
  wire [5:0] ir_1_alu_select_11_6;
  wire [11:0] adder_1_out, adder_2_out, ir_1_output_12bit, multiplexer_1_out, multiplexer_5_out,
       pc_1_pc_out12, regbankint_1_reg7sp, register_1_q;
  wire [15:0] alu_1_alu_output, multiplexer_4_out, regbankint_1_reg0, regbankint_1_reg1, regbankint_1_reg2,
       regbankint_1_reg3, regbankint_1_reg4, regbankint_1_reg5, regbankint_1_reg6;
  wire [15:12] multiplexer_5_out_2, regbankint_1_reg7sp_2;

  Multiplexer #(.width(12), .enable("false")) multiplexer_1 (
    .in0(adder_1_out), .in1(mem_out[11:0]), .out(multiplexer_1_out), .sel(RETMUX));
  Adder #(.width(12)) adder_1 (.a(pc_1_pc_out12), .b(ir_1_output_12bit), .out(adder_1_out));  // open: cin, cout
  PC pc_1 (.pc_in12(multiplexer_1_out), .pc_inc(PC_plus_plus), .pc_ld(PCLD), .clock(CLOCK), .pc_out12(pc_1_pc_out12));
  Multiplexer #(.select(2), .width(12), .enable("false")) multiplexer_2 (
    .in0(pc_1_pc_out12), .in1(multiplexer_5_out), .in2(regbankint_1_reg7sp), .in3(register_1_q),
    .out(mem_address), .sel(ARMUX));
  RegBankINT regbankint_1 (
    .data_in(mem_datain), .reg_sel(ir_1_dst_2_0), .regld(REGLD), .sp_plus_plus(SP_plus_plus),
    .sp_minus_minus(SP_minus_minus), .FLAGLD(FLAGLD), .clock(CLOCK), .CLI(CLI), .IF(regbankint_1_if),
    .ZF(regbankint_1_zf), .STI(STI), .ZFLD(ZFLD), .ZFlag_from_alu(alu_1_zeroflag_forreg),
    .Reg0(regbankint_1_reg0), .Reg1(regbankint_1_reg1), .Reg2(regbankint_1_reg2), .Reg3(regbankint_1_reg3),
    .Reg4(regbankint_1_reg4), .Reg5(regbankint_1_reg5), .Reg6(regbankint_1_reg6),
    .Reg7sp({regbankint_1_reg7sp_2, regbankint_1_reg7sp}));
  Multiplexer #(.select(3), .width(16), .enable("false")) multiplexer_3 (
    .in0(mem_out), .in1(multiplexer_4_out), .in2({multiplexer_5_out_2, multiplexer_5_out}),
    .in3(alu_1_alu_output), .in4({4'b0000, pc_1_pc_out12}), .in5(regbankint_1_reg6), .in6({16{1'b0}}),
    .in7({16{1'b0}}), .out(mem_datain), .sel(MUX));
  Multiplexer #(.select(3), .width(16), .enable("false")) multiplexer_4 (
    .in0(regbankint_1_reg0), .in1(regbankint_1_reg1), .in2(regbankint_1_reg2), .in3(regbankint_1_reg3),
    .in4(regbankint_1_reg4), .in5(regbankint_1_reg5), .in6(regbankint_1_reg6),
    .in7({regbankint_1_reg7sp_2, regbankint_1_reg7sp}), .out(multiplexer_4_out), .sel(ir_1_src_8_6));
  IR ir_1 (
    .input_12bit(mem_out[11:0]), .IRLD(IRLD), .CLK(CLOCK), .alu_select_11_6(ir_1_alu_select_11_6),
    .src_8_6(ir_1_src_8_6), .src_5_3(ir_1_src_5_3), .dst_2_0(ir_1_dst_2_0), .output_12bit(ir_1_output_12bit));
  ALU alu_1 (
    .ZeroFlag_forREG(alu_1_zeroflag_forreg), .input1(multiplexer_4_out),
    .input2({multiplexer_5_out_2, multiplexer_5_out}), .alu_output(alu_1_alu_output),
    .alu_sel(ir_1_alu_select_11_6));
  and and_1 (and_1_out, INT, regbankint_1_if);
  Multiplexer #(.select(3), .width(16), .enable("false")) multiplexer_5 (
    .in0(regbankint_1_reg0), .in1(regbankint_1_reg1), .in2(regbankint_1_reg2), .in3(regbankint_1_reg3),
    .in4(regbankint_1_reg4), .in5(regbankint_1_reg5), .in6(regbankint_1_reg6),
    .in7({regbankint_1_reg7sp_2, regbankint_1_reg7sp}), .out({multiplexer_5_out_2, multiplexer_5_out}),
    .sel(ir_1_src_5_3));
  interrupt_cu interrupt_cu_1 (
    .opcode(mem_out[15:12]), .IF_INT(and_1_out), .clock(CLOCK), .zf_fromReg(regbankint_1_zf), .MEMLD(MEMLD),
    .INTACK(INTACK), .ARMUX(ARMUX), .PCLD(PCLD), .PC_plus_plus(PC_plus_plus), .RETMUX(RETMUX),
    .SP_plus_plus(SP_plus_plus), .SP_minus_minus(SP_minus_minus), .FLAGLD(FLAGLD), .CLI(CLI), .STI(STI),
    .REGLD(REGLD), .ZFLD(ZFLD), .MUX(MUX), .IRLD(IRLD), .INT_LD(INTLD));  // open: nextaddress, FETCH
  Adder #(.width(12)) adder_2 (.a(mem_out[11:0]), .b(12'h64e), .out(adder_2_out));  // open: cin, cout
  Register #(.width(12)) register_1 (.D(adder_2_out), .en(INTLD), .Q(register_1_q), .clk(CLOCK));  // open: clr
endmodule

module counter (
  output [15:0] _16bitcounter,
  output equal1024,
  output [15:0] toplam
);

  wire [0:0] clock_1_out;
  wire [15:0] adder_1_out, adder_2_out, multiplexer_1_out, multiplexer_2_out, reg16bit_1__16bit_output;

  Clock clock_1 (.out(clock_1_out[0]));
  Adder #(.width(16)) adder_1 (.a(_16bitcounter), .b(16'h1), .out(adder_1_out));  // open: cin, cout
  Multiplexer #(.width(16), .enable("false")) multiplexer_1 (
    .in0({{15{1'b0}}, clock_1_out[0]}), .in1(adder_1_out), .out(multiplexer_1_out), .sel(1'b1));
  reg16bit reg16bit_1 (
    .regld(clock_1_out[0]), ._16bit_input(multiplexer_1_out), .clock(clock_1_out[0]),
    ._16bit_output(reg16bit_1__16bit_output));
  Adder #(.width(16)) adder_2 (.a(16'h1), .b(toplam), .out(adder_2_out));  // open: cin, cout
  Multiplexer #(.width(16), .enable("false")) multiplexer_2 (
    .in0(toplam), .in1(adder_2_out), .out(multiplexer_2_out), .sel(equal1024));
  Multiplexer #(.width(16), .enable("false")) multiplexer_3 (
    .in0(reg16bit_1__16bit_output), .in1({16{1'b0}}), .out(_16bitcounter), .sel(equal1024));
  Comparator #(.width(16)) comparator_1 (.a(reg16bit_1__16bit_output), .b(16'h400), .eq(equal1024));  // open: gt, lt
  reg16bit reg16bit_2 (
    .regld(clock_1_out[0]), ._16bit_input(multiplexer_2_out), .clock(clock_1_out[0]), ._16bit_output(toplam));
endmodule

module poll_int_clk (
  input  [15:0] PollingInput,
  input  ready,
  input  [15:0] InterruptInput
);

  wire _7SEG0, _7SEG1, and_1_out, B00_out, B01_out, clk_in, CLOCK, INT, INT_CS, INT_KPAD, INTACK, intCLK,
       led_2_ledout, MEM_0, MEMLD, POLL_CS;
  wire [2:0] enc3bit;
  wire [11:0] ADDRESS;
  wire [15:0] CLOCK_OUT, INT_INPUT, MEM0_out, MEM_DATAIN, MEM_OUT, multiplexer_1_out, PIC_OUT, POLL_INPUT,
       reg16bit_2__16bit_output, reg16bit_3__16bit_output;

  Clock clock_1 (.out(clk_in));
  Button button_1 (.out(INT_KPAD));
  and _900_901_POL (POLL_CS, ADDRESS[11], ~ADDRESS[10], ~ADDRESS[9], ADDRESS[8], ~ADDRESS[7], ~ADDRESS[6], ~ADDRESS[5], ~ADDRESS[4], ~ADDRESS[3], ~ADDRESS[2], ~ADDRESS[1]);  // AND_Gate
  counter counter_1 (.equal1024(intCLK), .toplam(CLOCK_OUT));  // open: _16bitcounter
  keypad keypad_1 (
    .keypad_in(PollingInput), .readyButton(ready), .CS(POLL_CS), .A0(ADDRESS[0]), .keypad_out(POLL_INPUT));  // open: keypadINT
  reg16bit reg16bit_1 (.regld(1'b1), ._16bit_input(InterruptInput), .clock(INT_KPAD), ._16bit_output(INT_INPUT));
  and A00_INT (INT_CS, ADDRESS[11], ~ADDRESS[10], ADDRESS[9], ~ADDRESS[8], ~ADDRESS[7], ~ADDRESS[6], ~ADDRESS[5], ~ADDRESS[4], ~ADDRESS[3], ~ADDRESS[2], ~ADDRESS[1], ~ADDRESS[0]);  // AND_Gate
  and and_1 (and_1_out, MEM_0, MEMLD);
  and D23_CLK (CLOCK, ADDRESS[11], ADDRESS[10], ~ADDRESS[9], ADDRESS[8], ~ADDRESS[7], ~ADDRESS[6], ADDRESS[5], ~ADDRESS[4], ~ADDRESS[3], ~ADDRESS[2], ADDRESS[1], ADDRESS[0]);  // AND_Gate
  RAM #(.addrWidth(12), .dataWidth(16), .bus("separate")) ram_1 (
    .addr(ADDRESS), .din(MEM_DATAIN), .data(MEM0_out), .str(and_1_out), .sel(1'b1), .clk(clk_in), .ld(1'b1),
    .clr(1'b0));
  not not_1 (MEM_0, ADDRESS[11]);
  PIC pic_1 (.IN1(INT_KPAD), .IN2(intCLK), .INT(INT), .dataOut(PIC_OUT));
  encoder encoder_1 (
    ._0(1'b1), ._1(POLL_CS), ._2(INT_CS), ._3(CLOCK), ._4(MEM_0), ._5(1'b0), ._6(1'b0), ._7(1'b0),
    .\output (enc3bit));
  and and_2 (_7SEG0, B00_out, MEMLD);
  and B00 (B00_out, ADDRESS[11], ~ADDRESS[10], ADDRESS[9], ADDRESS[8], ~ADDRESS[7], ~ADDRESS[6], ~ADDRESS[5], ~ADDRESS[4], ~ADDRESS[3], ~ADDRESS[2], ~ADDRESS[1], ~ADDRESS[0]);  // AND_Gate
  Multiplexer #(.select(3), .width(16), .enable("false")) multiplexer_1 (
    .in0({16{1'b1}}), .in1(POLL_INPUT), .in2(INT_INPUT), .in3(CLOCK_OUT), .in4(MEM0_out), .in5({16{1'b1}}),
    .in6({16{1'b1}}), .in7({16{1'b1}}), .out(multiplexer_1_out), .sel(enc3bit));
  interruptCPU interruptcpu_1 (
    .CLOCK(clk_in), .mem_out(MEM_OUT), .INT(INT), .mem_address(ADDRESS), .mem_datain(MEM_DATAIN),
    .MEMLD(MEMLD), .INTACK(INTACK));  // open: INTLD
  Multiplexer #(.width(16), .enable("false")) multiplexer_2 (
    .in0(multiplexer_1_out), .in1(PIC_OUT), .out(MEM_OUT), .sel(INTACK));
  and and_3 (_7SEG1, B01_out, MEMLD);
  and B01 (B01_out, ADDRESS[11], ~ADDRESS[10], ADDRESS[9], ADDRESS[8], ~ADDRESS[7], ~ADDRESS[6], ~ADDRESS[5], ~ADDRESS[4], ~ADDRESS[3], ~ADDRESS[2], ~ADDRESS[1], ADDRESS[0]);  // AND_Gate
  LED_part led_1 (.in(led_2_ledout));
  LED led_2 (.LedOut(led_2_ledout), .set(INT_CS), .clear(POLL_CS));
  reg16bit reg16bit_2 (
    .regld(_7SEG0), ._16bit_input(MEM_DATAIN), .clock(clk_in), ._16bit_output(reg16bit_2__16bit_output));
  reg16bit reg16bit_3 (
    .regld(_7SEG1), ._16bit_input(MEM_DATAIN), .clock(clk_in), ._16bit_output(reg16bit_3__16bit_output));
  Hex_Digit_Display hex_digit_display_1 (.value(reg16bit_2__16bit_output[15:12]));  // open: dp
  Hex_Digit_Display hex_digit_display_2 (.value(reg16bit_3__16bit_output[15:12]));  // open: dp
  Hex_Digit_Display hex_digit_display_3 (.value(reg16bit_3__16bit_output[11:8]));  // open: dp
  Hex_Digit_Display hex_digit_display_4 (.value(reg16bit_2__16bit_output[11:8]));  // open: dp
  Hex_Digit_Display hex_digit_display_5 (.value(reg16bit_2__16bit_output[7:4]));  // open: dp
  Hex_Digit_Display hex_digit_display_6 (.value(reg16bit_3__16bit_output[7:4]));  // open: dp
  Hex_Digit_Display hex_digit_display_7 (.value(reg16bit_2__16bit_output[3:0]));  // open: dp
  Hex_Digit_Display hex_digit_display_8 (.value(reg16bit_3__16bit_output[3:0]));  // open: dp

  // Other names for the same wires on the sheet: INT_A0 = ADDRESS[0]; POLL_A0 = ADDRESS[0]

  // Notes on the sheet:
  //   MEM 000 - 7FF
endmodule

// FLAG
module flag (
  input  CLI,
  input  Clock,
  input  [1:0] datain,
  input  FLAGLD,
  input  ZFLD,
  input  ZeroFlagFromAlu,
  input  STI,
  output [1:0] dataOut
);

  wire and_1_out, and_2_out, and_3_out, and_4_out, and_5_out, and_6_out, and_7_out, and_8_out, and_9_out,
       and_10_out, or_1_out, or_2_out, or_3_out, or_4_out;

  and and_1 (and_1_out, CLI, 1'b0);
  and and_2 (and_2_out, CLI, 1'b1);
  and and_3 (and_3_out, datain[1], FLAGLD);
  and and_4 (and_4_out, ~datain[1], FLAGLD);  // AND_Gate
  and and_5 (and_5_out, 1'b1, STI);
  and and_6 (and_6_out, 1'b0, STI);
  or or_1 (or_1_out, and_3_out, and_5_out, and_1_out);
  or or_2 (or_2_out, and_4_out, and_6_out, and_2_out);
  S_R_Flip_Flop s_r_ff_1 (.S(or_1_out), .clk(Clock), .R(or_2_out), .Q(dataOut[1]));  // open: Qn, preset, reset, en
  and and_7 (and_7_out, datain[0], FLAGLD);
  and and_8 (and_8_out, ~datain[0], FLAGLD);  // AND_Gate
  and and_9 (and_9_out, ZFLD, ZeroFlagFromAlu);
  or or_3 (or_3_out, and_7_out, and_9_out);
  or or_4 (or_4_out, and_8_out, and_10_out);
  and and_10 (and_10_out, ZFLD, ~ZeroFlagFromAlu);  // AND_Gate
  S_R_Flip_Flop s_r_ff_2 (.S(or_3_out), .clk(Clock), .R(or_4_out), .Q(dataOut[0]));  // open: Qn, preset, reset, en
endmodule

// enc
module encoder (
  input  _0,
  input  _1,
  input  _2,
  input  _3,
  input  _4,
  input  _5,
  input  _6,
  input  _7,
  output [2:0] \output 
);

  wire priority_encoder_1_gs;
  wire [2:0] priority_encoder_1_out;

  Priority_Encoder priority_encoder_1 (
    .in0(_0), .in1(_1), .in2(_2), .in3(_3), .in4(_4), .in5(_5), .in6(_6), .in7(_7),
    .out(priority_encoder_1_out), .gs(priority_encoder_1_gs));  // open: en_in, en_out
  Multiplexer #(.width(3), .enable("false")) multiplexer_1 (
    .in0(3'b000), .in1(priority_encoder_1_out), .out(\output ), .sel(priority_encoder_1_gs));
endmodule

module toplama (
  input  [15:0] \sonsayı ,
  output [15:0] toplam
);

  wire [15:0] adder_1_out, multiplier_1_out;

  Adder #(.width(16)) adder_1 (.a(\sonsayı ), .b(16'h1), .out(adder_1_out));  // open: cin, cout
  Multiplier #(.width(16)) multiplier_1 (.a(\sonsayı ), .b(adder_1_out), .out(multiplier_1_out));  // open: cin, cout
  Divider #(.width(16)) divider_1 (.a(multiplier_1_out), .b(16'h2), .out(toplam));  // open: upper, rem
endmodule

module LED (
  input  set,
  input  clear,
  output LedOut
);

  S_R_Flip_Flop s_r_ff_1 (.S(1'b1), .clk(set), .R(1'b0), .Q(LedOut), .reset(clear), .en(set));  // open: Qn, preset
endmodule
